# Fritzing sketch door-sensor (saved by Fritzing 0.9.10b)
breadboards: 1

parts:
  IC1 = AE-TYBLE16 (300mil) [part_number=K-12339 package="DIP (Dual Inline) [THT]"]
  C1 = Capacitor Polarized [package=cpol-radial-100uf-25v]
  Q1 = LTR-301 [package=ltr-301]
  R1 = Resistor [tolerance=±5% power=0.25 resistance=1k package=THT]
  S1 = Toggle Switch [package=THT]
  S5 = Reed switch [package=THT]
  J3 = female pin header, 6 pins [form="♀ (female)"]
  J5 = female pin header, 2 pins [form="♀ (female)"]
  J6 = female pin header, 2 pins [form="♀ (female)"]
  IC2 = IC, DIP package, 6 pins [chip_label=R3111N211A]
  LED1 = LED - 3mm [color="Red (633nm)" current=30mA package="3 mm [THT]"]
  R3 = Resistor [tolerance=±5% power=0.25 resistance=47 package=THT]
  LED2 = LED - 3mm [color="Green (565nm)" current=30mA package="3 mm [THT]"]
  R4 = Resistor [tolerance=±5% power=0.25 resistance=47 package=THT]
  BAT1 = Battery Holders [package=battcon_245mm]
  S6 = Toggle Switch [package=THT]
  S8 = Toggle Switch [package=THT]
  S9 = SWITCH-DPDT [package=os]
  R5 = Resistor [tolerance=±5% power=0.25 resistance=1 package=THT]
  J7 = female pin header, 2 pins [form="♀ (female)"]

nets:
  N1: IC1.DIP2, J3.pin2
  N2: IC1.DIP3, J3.pin3
  N3: IC1.DIP5, J3.pin5
  N4: IC1.DIP6, J3.pin6
  N5: IC1.DIP9, Q1.E, R1.Pin_0, S1.L1, S1.COM
  N6: IC1.DIP10, R4.Pin_0
  N7: IC1.DIP13, C1.-, R1.Pin_1, J3.pin4, J5.pin2, IC2.pin3, LED2.cathode, BAT1.-
  N8: IC1.DIP14, C1.+, Q1.C, S1.L2, J3.pin1, IC2.pin2, LED1.anode, S9.1, J7.pin2
  N9: S5.pin_1, J6.pin1, S6.L2, S8.COM
  N10: S5.pin_2, J6.pin2, S6.L1, S6.COM, S9.6, R5.Pin_1
  N11: J5.pin1, S8.L1
  N12: IC2.pin1, R3.Pin_1
  N13: LED1.cathode, R3.Pin_0
  N14: LED2.anode, R4.Pin_1
  N15: BAT1.+, S8.L2
  N16: S9.2, S9.3, S9.5, J7.pin1
  N17: S9.4, R5.Pin_0

custom parts:
  AE-TYBLE16 (300mil): AE-TYBLE16 BLE module whose MPU core is nRF51822 as 300mil (7.62mm) breadfriendly width, actual width is 8.0mm
